// Logisim project LALU.circ as structural Verilog: 1 circuit, main circuit main
module main (
  input  subtract,
  input  rst,
  input  [15:0] in_3,
  output [15:0] out_4,
  output [15:0] out_5
);

  wire clk;
  wire [15:0] csbasedaddsubtract_1_sum;

  Clock clock_1 (.out(clk));
  CSBasedAddSubtract csbasedaddsubtract_1 (
    .OP(subtract), .A(out_4), .B(out_5), .Sum(csbasedaddsubtract_1_sum));  // open: Overflow
  Register #(.width(16)) R0 (.D(csbasedaddsubtract_1_sum), .en(1'b1), .clk(clk), .Q(out_4), .clr(rst));
  Register #(.width(16)) R1 (.D(in_3), .en(1'b1), .clk(clk), .Q(out_5), .clr(rst));

  // Other names for the same wires on the sheet: R0[15:0] = out_4; R1[15:0] = out_5
endmodule
